# Fritzing sketch ESP8266FlashFritzing (saved by Fritzing 0.9.3b)
breadboards: 1

parts:
  U2 = ESP8266 WiFi Module [part_number=ESP8266]
  Bauteil1 = FTDI Basic Programmer

nets:
  N1: U2.RXD, Bauteil1.RXI
  N2: U2.CH_PD, Bauteil1.POWER
  GND: U2.GND, Bauteil1.GND
  N3: U2.TXD, Bauteil1.TXO

custom parts:
  ESP8266 WiFi Module: Generic WiFi Module based on the ESP8266 with onboard PCB antenna and UART communications
