# Fritzing sketch Halbautonomroboter Fritzing (saved by Fritzing 0.9.3b)
breadboards: 1

parts:
  Bauteil1 = Arduino Mega 2560 (Rev3)
  VCC1 = Battery block 9V  # not connected
  LM1 = RioRand LM2596
  MOTOR4 = 28BYJ-48 Stepper Motor
  MOTOR5 = 28BYJ-48 Stepper Motor
  X4 = X113647 Stepper Driver Board [part_number=X113647 package=board]
  X5 = X113647 Stepper Driver Board [part_number=X113647 package=board]
  VCC2 = Battery block 9V
  U1 = ESP8266 WiFi Module [part_number=ESP8266]
  J1 = Basic Servo
  hc-sr1 = hc-sr04
  GY1 = MPU-6050 Board GY-521 [form="♀ (female)" package=THT]
  J2 = Basic Servo
  J3 = Basic Servo
  J4 = Basic Servo
  J5 = Basic Servo

nets:
  N1: Bauteil1.A0, J2.pulse
  N2: Bauteil1.A1, J1.pulse
  N3: Bauteil1.A2, J5.pulse
  N4: Bauteil1.A3, J4.pulse
  N5: Bauteil1.A4, J3.pulse
  N6: Bauteil1.D21/SCL, GY1.pin3
  N7: Bauteil1.D20/SDA, GY1.pin4
  N8: Bauteil1.D19/RX1, U1.TXD
  N9: Bauteil1.D18/TX1, U1.RXD
  N10: Bauteil1.D13_PWM, hc-sr1.Echo
  N11: Bauteil1.D12_PWM, hc-sr1.Trig
  N12: Bauteil1.D11_PWM, X4.IN4
  N13: Bauteil1.D10_PWM, X4.IN3
  N14: Bauteil1.D9_PWM, X4.IN2
  N15: Bauteil1.D8_PWM, X4.IN1
  VCC: Bauteil1.3V3, J1.vcc, J2.vcc, J3.vcc, J4.vcc, J5.vcc
  GND: Bauteil1.GND, VCC2.-, J1.gnd, J2.gnd, J3.gnd, J4.gnd, J5.gnd
  N16: Bauteil1.VIN, VCC2.+
  N17: Bauteil1.D4_PWM, X5.IN1
  N18: Bauteil1.D5_PWM, X5.IN2
  N19: Bauteil1.D6_PWM, X5.IN3
  N20: Bauteil1.D7_PWM, X5.IN4
  N21: LM1.Pin_2, X4.+V, X5.+V, hc-sr1.VCC, GY1.pin1
  GND_2: LM1.Pin_3, X4.GND, X5.GND, hc-sr1.GND, GY1.pin2
  N22: MOTOR4.BLUE, X4.BLUE
  N23: MOTOR4.PINK, X4.PINK
  N24: MOTOR4.RED, X4.YELLOW
  N25: MOTOR4.ORANGE, X4.ORANGE
  N26: MOTOR4.YELLOW, X4.RED
  N27: MOTOR5.BLUE, X5.BLUE
  N28: MOTOR5.PINK, X5.PINK
  N29: MOTOR5.RED, X5.YELLOW
  N30: MOTOR5.ORANGE, X5.ORANGE
  N31: MOTOR5.YELLOW, X5.RED

custom parts:
  28BYJ-48 Stepper Motor: 28BYJ-48 gear-reduction stepper motor (small)
  X113647 Stepper Driver Board: A common stepper motor driver board based on ULN2003APG darlington array
  ESP8266 WiFi Module: Generic WiFi Module based on the ESP8266 with onboard PCB antenna and UART communications
  MPU-6050 Board GY-521: Acelerometro y Giroscopio MPU-6050 Board GY-521
